// Digital circuit hal_adder - Logic.dig as structural Verilog
module hal_adder___Logic (
  input  A,
  input  B,
  output Carry,
  output Sum
);

  xor xor_1 (Sum, A, B);
  and and_1 (Carry, A, B);
endmodule

/* Test case Testes:
A B Carry Sum
0 0   0    0
1 0   0    1
0 1   0    1
1 1   1    0
*/
