// Digital circuit half_adder - VHDL.dig as structural Verilog
module half_adder___VHDL (
  input  i_bit1,
  input  i_bit2,
  output o_carry,
  output o_sum
);

  half_adder #(.applicationType("GHDL")) u_half_adder (
    .i_bit1(i_bit1), .i_bit2(i_bit2), .o_sum(o_sum), .o_carry(o_carry));
endmodule

/* Code of half_adder:
library ieee;
use ieee.std_logic_1164.all;
use ieee.numeric_std.all;

entity half_adder is
port (
	i_bit1: in std_logic;
	i_bit2: in std_logic;
	o_sum: out std_logic;
	o_carry: out std_logic
     );
end half_adder;

architecture rtl of half_adder is
begin
	o_sum <= i_bit1 xor i_bit2;
	o_carry <= i_bit1 and i_bit2;
end rtl;
*/

/* Test case Testes:
i_bit1 i_bit2 o_carry o_sum
   0      0       0      0
   1      0       0      1
   0      1       0      1
   1      1       1      0
*/
